// Logisim project Lab1_Problem1_Circuits.circ as structural Verilog: 1 circuit, main circuit main
module main (
);

  wire clock_1_out, clock_2_out, clock_3_out, clock_4_out, clock_5_out, clock_6_out, clock_7_out,
       clock_8_out, clock_9_out, not_1_out, not_2_out;

  Clock clock_1 (.out(clock_1_out));
  Clock clock_2 (.out(clock_2_out));
  Clock clock_3 (.out(clock_3_out));
  Clock clock_4 (.out(clock_4_out));
  Clock clock_5 (.out(clock_5_out));
  Clock clock_6 (.out(clock_6_out));
  Clock clock_7 (.out(clock_7_out));
  Clock clock_8 (.out(clock_8_out));
  Clock clock_9 (.out(clock_9_out));
  not not_1 (not_1_out, clock_6_out);
  not not_2 (not_2_out, clock_9_out);

  // Notes on the sheet:
  //   A
  //   B
  //   C
  //   A
  //   B
  //   C
  //   A
  //   B
  //   C
  //   Circuit for X Equation
  //   Circuit For Y Equation
  //   X = C
  //   Combined Circuit For Both Outputs
  //   Y = C'
  //   X = C
  //   Y = C'
endmodule
