// Logisim project Lab1_Problem2_Circuits.circ as structural Verilog: 1 circuit, main circuit main
module main (
);

  wire and_1_out, and_2_out, and_3_out, and_4_out, clock_1_out, clock_2_out, clock_3_out, clock_4_out,
       clock_5_out, clock_6_out, clock_7_out, clock_8_out, clock_9_out, clock_10_out, clock_11_out,
       clock_12_out, clock_13_out, clock_14_out, clock_15_out, clock_16_out, clock_17_out, clock_18_out,
       clock_19_out, clock_20_out, clock_21_out, clock_22_out, clock_23_out, clock_24_out, clock_25_out,
       clock_26_out, clock_27_out, clock_28_out, nand_1_out, nand_2_out, nand_3_out, nand_4_out, nand_5_out,
       nand_6_out, nand_7_out, nand_8_out, nand_9_out, nand_10_out, nand_11_out, nand_12_out, nand_13_out,
       nand_14_out, nand_15_out, nand_16_out, nand_17_out, nand_18_out, nand_19_out, nand_20_out,
       nand_21_out, nand_22_out, nand_23_out, nand_24_out, nand_25_out, nand_26_out, nand_27_out,
       nand_28_out, nand_29_out, nand_30_out, nand_31_out, nand_32_out, nand_33_out, nand_34_out, not_1_out,
       not_2_out, not_3_out, not_4_out, not_5_out, not_6_out, not_7_out, not_8_out, or_1_out;

  Clock #(.phaseOffset(1)) clock_1 (.out(clock_1_out));
  Clock clock_2 (.out(clock_2_out));
  Clock clock_3 (.out(clock_3_out));
  Clock clock_4 (.out(clock_4_out));
  Clock #(.phaseOffset(1)) clock_5 (.out(clock_5_out));
  Clock clock_6 (.out(clock_6_out));
  Clock clock_7 (.out(clock_7_out));
  Clock clock_8 (.out(clock_8_out));
  Clock clock_9 (.out(clock_9_out));
  Clock clock_10 (.out(clock_10_out));
  Clock clock_11 (.out(clock_11_out));
  Clock clock_12 (.out(clock_12_out));
  not not_1 (not_1_out, clock_1_out);
  not not_2 (not_2_out, clock_6_out);
  not not_3 (not_3_out, clock_7_out);
  not not_4 (not_4_out, clock_8_out);
  not not_5 (not_5_out, clock_9_out);
  not not_6 (not_6_out, clock_10_out);
  not not_7 (not_7_out, clock_11_out);
  not not_8 (not_8_out, clock_12_out);
  and and_1 (and_1_out, not_1_out, clock_2_out, clock_3_out);
  and and_2 (and_2_out, clock_5_out, not_2_out, not_3_out);
  and and_3 (and_3_out, clock_5_out, not_2_out, not_4_out);
  and and_4 (and_4_out, not_5_out, not_6_out, not_7_out, not_8_out);
  or or_1 (or_1_out, and_2_out, and_3_out);
  Clock #(.phaseOffset(1)) clock_13 (.out(clock_13_out));
  Clock clock_14 (.out(clock_14_out));
  Clock clock_15 (.out(clock_15_out));
  Clock clock_16 (.out(clock_16_out));
  Clock clock_17 (.out(clock_17_out));
  Clock clock_18 (.out(clock_18_out));
  Clock clock_19 (.out(clock_19_out));
  Clock clock_20 (.out(clock_20_out));
  Clock #(.phaseOffset(1)) clock_21 (.out(clock_21_out));
  Clock clock_22 (.out(clock_22_out));
  Clock clock_23 (.out(clock_23_out));
  Clock clock_24 (.out(clock_24_out));
  Clock #(.phaseOffset(1)) clock_25 (.out(clock_25_out));
  Clock clock_26 (.out(clock_26_out));
  Clock clock_27 (.out(clock_27_out));
  Clock clock_28 (.out(clock_28_out));
  nand nand_1 (nand_1_out, clock_25_out, clock_25_out);
  nand nand_2 (nand_2_out, clock_17_out, clock_17_out);
  nand nand_3 (nand_3_out, clock_18_out, clock_18_out);
  nand nand_4 (nand_4_out, clock_19_out, clock_19_out);
  nand nand_5 (nand_5_out, clock_20_out, clock_20_out);
  nand nand_6 (nand_6_out, nand_1_out, clock_26_out, clock_27_out);
  nand nand_7 (nand_7_out, clock_14_out, clock_14_out);
  nand nand_8 (nand_8_out, clock_15_out, clock_15_out);
  nand nand_9 (nand_9_out, clock_16_out, clock_16_out);
  nand nand_10 (nand_10_out, clock_21_out, clock_21_out);
  nand nand_11 (nand_11_out, clock_22_out, clock_22_out);
  nand nand_12 (nand_12_out, clock_23_out, clock_23_out);
  nand nand_13 (nand_13_out, clock_24_out, clock_24_out);
  nand nand_14 (nand_14_out, clock_13_out, nand_7_out, nand_8_out);
  nand nand_15 (nand_15_out, clock_13_out, nand_7_out, nand_9_out);
  nand nand_16 (nand_16_out, nand_2_out, nand_3_out, nand_4_out, nand_5_out);
  nand nand_17 (nand_17_out, nand_6_out, nand_6_out);
  nand nand_18 (nand_18_out, nand_10_out, clock_22_out, clock_23_out);
  nand nand_19 (nand_19_out, clock_21_out, nand_11_out, nand_12_out);
  nand nand_20 (nand_20_out, clock_21_out, nand_11_out, nand_13_out);
  nand nand_21 (nand_21_out, nand_10_out, nand_11_out, nand_12_out, nand_13_out);
  nand nand_22 (nand_22_out, nand_14_out, nand_14_out);
  nand nand_23 (nand_23_out, nand_15_out, nand_15_out);
  nand nand_24 (nand_24_out, nand_16_out, nand_16_out);
  nand nand_25 (nand_25_out, nand_18_out, nand_18_out);
  nand nand_26 (nand_26_out, nand_19_out, nand_19_out);
  nand nand_27 (nand_27_out, nand_20_out, nand_20_out);
  nand nand_28 (nand_28_out, nand_21_out, nand_21_out);
  nand nand_29 (nand_29_out, nand_22_out, nand_22_out);
  nand nand_30 (nand_30_out, nand_23_out, nand_23_out);
  nand nand_31 (nand_31_out, nand_26_out, nand_26_out);
  nand nand_32 (nand_32_out, nand_27_out, nand_27_out);
  nand nand_33 (nand_33_out, nand_29_out, nand_30_out);
  nand nand_34 (nand_34_out, nand_31_out, nand_32_out);

  // Notes on the sheet:
  //   A
  //   B
  //   C
  //   D
  //   A
  //   B
  //   C
  //   D
  //   A
  //   B
  //   C
  //   D
  //   Circuit For X Equation
  //   Circuit For Y Equation
  //   Circuit For Z Equation
  //   X=A'BC
  //   Z=A'B'C'D'
  //   Y=AB'C'+AB'D'
  //   A
  //   B
  //   C
  //   D
  //   A
  //   B
  //   C
  //   D
  //   A
  //   B
  //   C
  //   D
  //   A
  //   B
  //   C
  //   D
  //   For X Equation
  //   For Y Equation
  //   For Z Equation
  //   Circuits Using Only NAND Gates
  //   Common Circuit Reusing Segments of Previous Circuits
  //   X=A'BC
  //   Z=A'B'C'D'
  //   X=A'BC
  //   Z=A'B'C'D'
  //   Y=AB'C'+AB'D'
  //   Y=AB'C'+AB'D'
endmodule
