// Logisim project Lab1_Problem3_Circuits.circ as structural Verilog: 1 circuit, main circuit main
module main (
);

  wire and_1_out, and_2_out, and_3_out, clock_1_out, clock_2_out, clock_3_out, clock_4_out, clock_5_out,
       clock_6_out, nand_1_out, not_1_out, not_2_out, or_1_out, or_2_out, xor_1_out;

  Clock #(.phaseOffset(1)) clock_1 (.out(clock_1_out));
  Clock clock_2 (.out(clock_2_out));
  Clock #(.phaseOffset(1)) clock_3 (.out(clock_3_out));
  Clock clock_4 (.out(clock_4_out));
  Clock #(.phaseOffset(1)) clock_5 (.out(clock_5_out));
  Clock clock_6 (.out(clock_6_out));
  not not_1 (not_1_out, clock_1_out);
  not not_2 (not_2_out, clock_2_out);
  nand nand_1 (nand_1_out, clock_3_out, clock_4_out);
  or or_1 (or_1_out, clock_3_out, clock_4_out);
  xor xor_1 (xor_1_out, clock_5_out, clock_6_out);
  and and_1 (and_1_out, not_1_out, clock_2_out);
  and and_2 (and_2_out, clock_1_out, not_2_out);
  and and_3 (and_3_out, nand_1_out, or_1_out);
  or or_2 (or_2_out, and_1_out, and_2_out);

  // Notes on the sheet:
  //   A
  //   B
  //   A
  //   B
  //   A
  //   B
  //   Circuit For Equation X
  //   Reduced Circuit For Equation For X
  //   Reduced Circuit For Equation X Implementing XOR Gate
  //   X=A'B+AB'
  //   X=A'B+AB'
  //   X=A'B+AB'
endmodule
