// Logisim project Lab1_Problem4_Circuits.circ as structural Verilog: 1 circuit, main circuit main
module main (
);

  wire and_1_out, and_2_out, and_3_out, and_4_out, and_5_out, and_6_out, clock_1_out, clock_2_out,
       clock_3_out, clock_4_out, clock_6_out, clock_7_out, clock_8_out, clock_9_out, clock_10_out,
       clock_11_out, clock_12_out, not_1_out, not_2_out, not_3_out, not_4_out, or_1_out, or_2_out, or_3_out,
       or_4_out;

  Clock #(.phaseOffset(1)) clock_1 (.out(clock_1_out));
  Clock clock_2 (.out(clock_2_out));
  Clock clock_3 (.out(clock_3_out));
  Clock clock_4 (.out(clock_4_out));
  Clock clock_5 ();  // open: out
  Clock #(.phaseOffset(1)) clock_6 (.out(clock_6_out));
  Clock clock_7 (.out(clock_7_out));
  Clock clock_8 (.out(clock_8_out));
  Clock clock_9 (.out(clock_9_out));
  Clock #(.phaseOffset(1)) clock_10 (.out(clock_10_out));
  Clock clock_11 (.out(clock_11_out));
  Clock clock_12 (.out(clock_12_out));
  and and_1 (and_1_out, clock_2_out, clock_3_out);
  not not_1 (not_1_out, clock_6_out);
  not not_2 (not_2_out, clock_7_out);
  and and_2 (and_2_out, not_1_out, clock_7_out);
  and and_3 (and_3_out, clock_6_out, not_2_out);
  not not_3 (not_3_out, clock_11_out);
  not not_4 (not_4_out, clock_10_out);
  or or_1 (or_1_out, clock_1_out, and_1_out);
  and and_4 (and_4_out, clock_10_out, clock_11_out);
  or or_2 (or_2_out, and_2_out, and_3_out);
  or or_3 (or_3_out, clock_9_out, and_4_out);
  and and_5 (and_5_out, clock_10_out, not_3_out);
  and and_6 (and_6_out, clock_11_out, not_4_out);
  or or_4 (or_4_out, and_5_out, and_6_out);

  // Notes on the sheet:
  //   A
  //   C
  //   D
  //   A
  //   C
  //   D
  //   A
  //   B
  //   C
  //   D
  //   Circuit For Equation X
  //   B
  //   Circuit For Equation Y
  //   B
  //   Combined Circuit
  //   X=A+BC
  //   Y=BC'+B'C
  //   X=A+BC
  //   Y=BC'+B'C
endmodule
