// Logisim project fiscsim.circ as structural Verilog: 1 circuit, main circuit main
module main (
);

  wire and_1_out, and_2_out, CLK, d_ff_1_q, decoder_1_out0, decoder_1_out1, decoder_1_out2, decoder_1_out3,
       nor_1_out, not_1_out, not_2_out;
  wire [5:0] multiplexer_1_out, register_1_q, rom_1_data, subtractor_1_out;
  wire [7:0] adder_1_out, and_3_out, multiplexer_2_out, multiplexer_3_out, multiplexer_4_out, not_3_out,
       register_2_q, register_3_q, register_4_q, register_5_q;
  wire [7:6] rom_1_data_2;

  Register #(.width(6)) register_1 (.D(multiplexer_1_out), .Q(register_1_q), .clk(CLK));  // open: en, clr
  Multiplexer #(.width(6), .enable("false")) multiplexer_1 (
    .in0(subtractor_1_out), .in1(rom_1_data), .out(multiplexer_1_out), .sel(and_1_out));
  Subtractor #(.width(6)) subtractor_1 (.a(register_1_q), .b({6{1'b1}}), .out(subtractor_1_out));  // open: bin, bout
  ROM #(.addrWidth(6)) rom_1 (.addr(register_1_q), .data({rom_1_data_2, rom_1_data}));  // open: sel
  and and_1 (and_1_out, and_2_out, not_1_out);
  not not_1 (not_1_out, d_ff_1_q);
  not not_2 (not_2_out, and_2_out);
  Decoder #(.select(2)) decoder_1 (
    .out0(decoder_1_out0), .out1(decoder_1_out1), .out2(decoder_1_out2), .out3(decoder_1_out3),
    .sel(rom_1_data[1:0]), .en(not_2_out));
  and and_2 (and_2_out, rom_1_data_2[6], rom_1_data_2[7]);
  D_Flip_Flop d_ff_1 (.clk(CLK), .D(nor_1_out), .Q(d_ff_1_q), .en(not_2_out));  // open: Qn, preset, reset
  Register register_2 (.D(multiplexer_4_out), .en(decoder_1_out0), .Q(register_2_q), .clk(CLK));  // open: clr
  Register register_3 (.D(multiplexer_4_out), .en(decoder_1_out1), .Q(register_3_q), .clk(CLK));  // open: clr
  Register register_4 (.D(multiplexer_4_out), .en(decoder_1_out2), .Q(register_4_q), .clk(CLK));  // open: clr
  Register register_5 (.D(multiplexer_4_out), .en(decoder_1_out3), .Q(register_5_q), .clk(CLK));  // open: clr
  Clock clock_1 (.out(CLK));
  Multiplexer #(.select(2), .width(8), .enable("false")) multiplexer_2 (
    .in0(register_2_q), .in1(register_3_q), .in2(register_4_q), .in3(register_5_q), .out(multiplexer_2_out),
    .sel(rom_1_data[5:4]));
  Multiplexer #(.select(2), .width(8), .enable("false")) multiplexer_3 (
    .in0(register_2_q), .in1(register_3_q), .in2(register_4_q), .in3(register_5_q), .out(multiplexer_3_out),
    .sel(rom_1_data[3:2]));
  Hex_Digit_Display hex_digit_display_1 (.value(register_5_q[7:4]));  // open: dp
  Hex_Digit_Display hex_digit_display_2 (.value(register_5_q[3:0]));  // open: dp
  nor nor_1 (nor_1_out, multiplexer_4_out[0], multiplexer_4_out[1], multiplexer_4_out[2], multiplexer_4_out[3], multiplexer_4_out[4], multiplexer_4_out[5], multiplexer_4_out[6], multiplexer_4_out[7]);
  Adder adder_1 (.a(multiplexer_2_out), .b(multiplexer_3_out), .out(adder_1_out));  // open: cin, cout
  assign and_3_out = multiplexer_2_out & multiplexer_3_out;  // AND_Gate and_3, 8 bits wide
  assign not_3_out = ~multiplexer_2_out;  // NOT_Gate not_3, 8 bits wide
  Multiplexer #(.select(2), .width(8)) multiplexer_4 (
    .in0(adder_1_out), .in1(and_3_out), .in2(not_3_out), .out(multiplexer_4_out), .sel(rom_1_data_2),
    .en(not_2_out));  // open: in3
endmodule
