// Logisim project miscsim.circ as structural Verilog: 6 circuits, main circuit main
module main (
);

  wire and_1_out, and_2_out, and_3_out, and_4_out, and_5_out, and_6_out, CLK, controller_1_bcs,
       controller_1_bnz, controller_1_data, controller_1_st, display_decoder_1_f0, display_decoder_1_f1,
       n7_segment_display_1_p1, n7_segment_display_1_p2, n7_segment_display_2_p2, n7_segment_display_5_p1,
       n7_segment_display_5_p2, n7_segment_display_6_p2, nor_1_out, or_1_out, or_2_out;
  wire [1:0] alu_1_z, controller_1_mvi, controller_1_rd, controller_1_rm, controller_1_rn, Status_Register_q;
  wire [3:0] alu_1_output_a_2, controller_1_aluop;
  wire [7:0] adder_1_out, controller_1_immediate, multiplexer_2_out, multiplexer_3_out, ram_1_dout,
       register_3_q, register_4_q, register_file_1_output_a, register_file_1_output_b,
       register_file_1_output_c, xor_1_out;
  wire [7:4] alu_1_output_a;
  wire [9:0] controller_1_address;
  wire [11:0] register_2_q, rom_1_data;
  wire [12:0] bit_extender_1_out, multiplexer_1_out, register_1_q, subtractor_1_out;

  Multiplexer #(.width(13)) multiplexer_1 (
    .in0(subtractor_1_out), .in1(bit_extender_1_out), .out(multiplexer_1_out), .sel(or_1_out));
  Register #(.width(13)) register_1 (.D(multiplexer_1_out), .clk(CLK), .Q(register_1_q));  // open: en, clr
  Clock clock_1 (.out(CLK));
  Subtractor #(.width(13)) subtractor_1 (.a(register_1_q), .b({13{1'b1}}), .out(subtractor_1_out));  // open: bin, bout
  ROM #(.addrWidth(13), .dataWidth(12)) rom_1 (.addr(register_1_q), .data(rom_1_data));
  assign bit_extender_1_out = {{3{controller_1_address[9]}}, controller_1_address};  // Bit_Extender bit_extender_1
  Register #(.width(12)) register_2 (.D(rom_1_data), .en(1'b1), .clk(CLK), .Q(register_2_q));  // open: clr
  or or_1 (or_1_out, and_1_out, and_2_out);
  and and_1 (and_1_out, controller_1_bnz, ~Status_Register_q[0]);  // AND_Gate
  and and_2 (and_2_out, controller_1_bcs, Status_Register_q[1]);
  Controller controller_1 (
    .input_a(register_2_q), .Rd(controller_1_rd), .Rm(controller_1_rm), .Rn(controller_1_rn),
    .ALUop(controller_1_aluop), .Data(controller_1_data), .BNZ(controller_1_bnz), .BCS(controller_1_bcs),
    .MVI(controller_1_mvi[0]), .Address(controller_1_address), .Immediate(controller_1_immediate),
    .ST(controller_1_st), .LD(controller_1_mvi[1]));
  Multiplexer #(.select(2), .width(8)) multiplexer_2 (
    .in0({alu_1_output_a, alu_1_output_a_2}), .in1(controller_1_immediate), .in2(ram_1_dout),
    .out(multiplexer_2_out), .sel(controller_1_mvi));  // open: in3
  or or_2 (or_2_out, controller_1_data, controller_1_mvi[0]);
  and and_3 (and_3_out, alu_1_output_a[7], alu_1_output_a[6], ~controller_1_mvi[1], alu_1_output_a[5], alu_1_output_a[4]);  // AND_Gate
  RAM #(.asyncread("true")) ram_1 (
    .addr({alu_1_output_a, alu_1_output_a_2}), .we(controller_1_st), .oe(controller_1_mvi[1]), .clk(CLK),
    .din(register_file_1_output_c), .dout(ram_1_dout));
  nor nor_1 (nor_1_out, register_1_q[0], register_1_q[1], register_1_q[2], register_1_q[3], register_1_q[4], register_1_q[5], register_1_q[6], register_1_q[7], register_1_q[8], register_1_q[9], register_1_q[10], register_1_q[11], register_1_q[12]);
  and and_4 (and_4_out, or_2_out, ~nor_1_out, ~controller_1_st);  // AND_Gate
  Display_Decoder display_decoder_1 (
    .En(and_3_out), .input_a(alu_1_output_a_2), .F1(display_decoder_1_f1), .F0(display_decoder_1_f0));  // open: FF, FE, FD, FC, FB, FA, F9, F8, F7, F6, F5, F4, F3, F2
  and and_5 (and_5_out, controller_1_st, display_decoder_1_f0);
  Register_File register_file_1 (
    .WDn(multiplexer_2_out), .CLK(CLK), .RAn(controller_1_rm), .WAn(and_4_out), .Rd(controller_1_rd),
    .Rdn(controller_1_rn), .Rnn(controller_1_rd), .output_a(register_file_1_output_a),
    .output_b(register_file_1_output_b), .output_c(register_file_1_output_c));
  Register register_3 (.D(register_file_1_output_c), .en(and_5_out), .clk(CLK), .Q(register_3_q));  // open: clr
  and and_6 (and_6_out, controller_1_st, display_decoder_1_f1);
  ALU alu_1 (
    .A(register_file_1_output_a), .B(register_file_1_output_b), .ALUop(controller_1_aluop),
    .cout(alu_1_z[1]), .output_a({alu_1_output_a, alu_1_output_a_2}), .Z(alu_1_z[0]));
  // _7_Segment_Display 7_segment_display_1: pin names not known; wires that end beside it: n7_segment_display_1_p1, n7_segment_display_1_p2
  // _7_Segment_Display 7_segment_display_2: pin names not known; wires that end beside it: n7_segment_display_1_p2, n7_segment_display_2_p2
  // BCD_to_7_Segment_decoder bcd_to_7_segment_decoder_1: pin names not known
  // BCD_to_7_Segment_decoder bcd_to_7_segment_decoder_2: pin names not known
  // Binary_to_BCD_converter #(.binvalue(8)) binary_to_bcd_converter_1: pin names not known; wires that end beside it: register_3_q, n7_segment_display_1_p1, n7_segment_display_1_p2
  _7_Segment_Display u_7_segment_display_3 ();  // open: g, f, a, b, e, d, c, dp
  // BCD_to_7_Segment_decoder bcd_to_7_segment_decoder_3: pin names not known; wires that end beside it: n7_segment_display_2_p2
  Register #(.width(2)) Status_Register (.D(alu_1_z), .en(and_4_out), .clk(CLK), .Q(Status_Register_q));  // open: clr
  Register register_4 (.D(register_file_1_output_c), .en(and_6_out), .clk(CLK), .Q(register_4_q));  // open: clr
  assign xor_1_out = {8{1'b1}} ^ register_4_q;  // XOR_Gate xor_1, 8 bits wide
  Multiplexer #(.width(8)) multiplexer_3 (
    .in0(register_4_q), .in1(adder_1_out), .out(multiplexer_3_out), .sel(register_4_q[7]));
  Adder adder_1 (.a(8'h1), .b(xor_1_out), .out(adder_1_out));  // open: cin, cout
  _7_Segment_Display u_7_segment_display_4 (.g(register_4_q[7]));  // open: f, a, b, e, d, c, dp
  // _7_Segment_Display 7_segment_display_5: pin names not known; wires that end beside it: n7_segment_display_5_p1, n7_segment_display_5_p2
  // BCD_to_7_Segment_decoder bcd_to_7_segment_decoder_4: pin names not known
  // Binary_to_BCD_converter #(.binvalue(8)) binary_to_bcd_converter_2: pin names not known; wires that end beside it: multiplexer_3_out, n7_segment_display_5_p1, n7_segment_display_5_p2
  // _7_Segment_Display 7_segment_display_6: pin names not known; wires that end beside it: n7_segment_display_5_p2, n7_segment_display_6_p2
  // BCD_to_7_Segment_decoder bcd_to_7_segment_decoder_5: pin names not known
  _7_Segment_Display u_7_segment_display_7 ();  // open: g, f, a, b, e, d, c, dp
  // BCD_to_7_Segment_decoder bcd_to_7_segment_decoder_6: pin names not known; wires that end beside it: n7_segment_display_6_p2

  // Notes on the sheet:
  //   contents of rom_1 (hex, n*v repeats v):
  //   341 dff dc6 3b 330 dff dca 3b 331 c07 c 400
  //   Fahrenheit
  //   Celsius
endmodule

module Register_File (
  input  [7:0] WDn,
  input  CLK,
  input  [1:0] RAn,
  input  WAn,
  input  [1:0] Rd,
  input  [1:0] Rdn,
  input  [1:0] Rnn,
  output [7:0] output_a,
  output [7:0] output_b,
  output [7:0] output_c
);

  wire decoder_1_out0, decoder_1_out1, decoder_1_out2, decoder_1_out3;
  wire [7:0] R0_q, R1_q, R2_q, R3_q;

  Decoder #(.select(2)) decoder_1 (
    .out0(decoder_1_out0), .out1(decoder_1_out1), .out2(decoder_1_out2), .out3(decoder_1_out3), .sel(Rd),
    .en(WAn));
  Register R0 (.D(WDn), .en(decoder_1_out0), .clk(CLK), .Q(R0_q));  // open: clr
  Register R1 (.D(WDn), .en(decoder_1_out1), .clk(CLK), .Q(R1_q));  // open: clr
  Register R2 (.D(WDn), .en(decoder_1_out2), .clk(CLK), .Q(R2_q));  // open: clr
  Register R3 (.D(WDn), .en(decoder_1_out3), .clk(CLK), .Q(R3_q));  // open: clr
  Multiplexer #(.select(2), .width(8)) multiplexer_1 (
    .in0(R0_q), .in1(R1_q), .in2(R2_q), .in3(R3_q), .out(output_a), .sel(RAn));
  Multiplexer #(.select(2), .width(8)) multiplexer_2 (
    .in0(R0_q), .in1(R1_q), .in2(R2_q), .in3(R3_q), .out(output_b), .sel(Rdn));
  Multiplexer #(.select(2), .width(8)) multiplexer_3 (
    .in0(R0_q), .in1(R1_q), .in2(R2_q), .in3(R3_q), .out(output_c), .sel(Rnn));
endmodule

module FourBitCLA (
  input  cin,
  input  [3:0] A,
  input  [3:0] B,
  output [3:0] Sum,
  output cout
);

  wire and_1_out, and_2_out, and_3_out, and_4_out, and_5_out, and_6_out, and_7_out, and_8_out, and_9_out,
       and_10_out, and_11_out, and_12_out, and_13_out, and_14_out, nand_1_out, nand_2_out, nand_3_out,
       nand_4_out, nor_1_out, nor_2_out, nor_3_out, nor_4_out, nor_5_out, nor_6_out, nor_7_out, not_1_out,
       not_2_out;

  not not_1 (not_1_out, cin);
  nor nor_1 (nor_1_out, A[0], B[0]);
  nand nand_1 (nand_1_out, A[0], B[0]);
  nor nor_2 (nor_2_out, A[1], B[1]);
  nand nand_2 (nand_2_out, A[1], B[1]);
  nor nor_3 (nor_3_out, A[2], B[2]);
  nand nand_3 (nand_3_out, A[2], B[2]);
  nor nor_4 (nor_4_out, A[3], B[3]);
  nand nand_4 (nand_4_out, A[3], B[3]);
  not not_2 (not_2_out, not_1_out);
  and and_1 (and_1_out, ~nor_1_out, nand_1_out);  // AND_Gate
  and and_2 (and_2_out, not_1_out, nand_1_out);
  and and_3 (and_3_out, ~nor_2_out, nand_2_out);  // AND_Gate
  and and_4 (and_4_out, not_1_out, nand_1_out, nand_2_out);
  and and_5 (and_5_out, nor_1_out, nand_2_out);
  and and_6 (and_6_out, ~nor_3_out, nand_3_out);  // AND_Gate
  and and_7 (and_7_out, not_1_out, nand_1_out, nand_2_out, nand_3_out);
  and and_8 (and_8_out, nor_1_out, nand_2_out, nand_3_out);
  and and_9 (and_9_out, nand_3_out, nor_2_out);
  and and_10 (and_10_out, ~nor_4_out, nand_4_out);  // AND_Gate
  and and_11 (and_11_out, not_1_out, nand_1_out, nand_2_out, nand_3_out, nand_4_out);
  and and_12 (and_12_out, nand_2_out, nand_3_out, nand_4_out, nor_1_out);
  and and_13 (and_13_out, nand_3_out, nand_4_out, nor_2_out);
  and and_14 (and_14_out, nand_4_out, nor_3_out);
  nor nor_5 (nor_5_out, nor_1_out, and_2_out);
  nor nor_6 (nor_6_out, nor_2_out, and_4_out, and_5_out);
  nor nor_7 (nor_7_out, nor_3_out, and_7_out, and_8_out, and_9_out);
  nor nor_8 (cout, and_11_out, and_12_out, and_13_out, and_14_out, nor_4_out);
  xor xor_1 (Sum[0], not_2_out, and_1_out);
  xor xor_2 (Sum[1], nor_5_out, and_3_out);
  xor xor_3 (Sum[2], nor_6_out, and_6_out);
  xor xor_4 (Sum[3], nor_7_out, and_10_out);
endmodule

module Controller (
  input  [11:0] input_a,
  output [1:0] Rd,
  output [1:0] Rm,
  output [1:0] Rn,
  output [3:0] ALUop,
  output Data,
  output BNZ,
  output BCS,
  output MVI,
  output [9:0] Address,
  output [7:0] Immediate,
  output ST,
  output LD
);

  and and_1 (ST, input_a[9], input_a[8], ~input_a[7], ~input_a[6]);  // AND_Gate
  and and_2 (Data, ~input_a[10], ~input_a[11]);  // AND_Gate
  and and_3 (BNZ, input_a[10], ~input_a[11]);  // AND_Gate
  and and_4 (LD, input_a[9], input_a[8], ~input_a[7], input_a[6]);  // AND_Gate
  and and_5 (MVI, input_a[10], input_a[11]);
  and and_6 (BCS, ~input_a[10], input_a[11]);  // AND_Gate

  assign Address = input_a[9:0];
  assign ALUop = input_a[9:6];
  assign Immediate = input_a[9:2];
  assign Rd = input_a[1:0];
  assign Rm = input_a[3:2];
  assign Rn = input_a[5:4];
endmodule

module ALU (
  input  [7:0] A,
  input  [7:0] B,
  input  [3:0] ALUop,
  output cout,
  output [7:0] output_a,
  output Z
);

  wire fourbitcla_1_cout, multiplexer_2_out;
  wire [3:0] fourbitcla_1_sum, fourbitcla_2_sum;
  wire [7:0] and_1_out, multiplexer_1_out, not_1_out, or_1_out, xor_1_out;

  assign xor_1_out = {8{1'b1}} ^ B;  // XOR_Gate xor_1, 8 bits wide
  Multiplexer #(.width(8)) multiplexer_1 (.in0(B), .in1(xor_1_out), .out(multiplexer_1_out), .sel(ALUop[0]));
  Multiplexer multiplexer_2 (.in0(1'b0), .in1(1'b1), .out(multiplexer_2_out), .sel(ALUop[0]));
  assign not_1_out = ~B;  // NOT_Gate not_1, 8 bits wide
  assign and_1_out = A & B;  // AND_Gate and_1, 8 bits wide
  assign or_1_out = A | B;  // OR_Gate or_1, 8 bits wide
  FourBitCLA fourbitcla_1 (
    .cin(multiplexer_2_out), .A(A[3:0]), .B(multiplexer_1_out[3:0]), .Sum(fourbitcla_1_sum),
    .cout(fourbitcla_1_cout));
  FourBitCLA fourbitcla_2 (
    .cin(fourbitcla_1_cout), .A(A[7:4]), .B(multiplexer_1_out[7:4]), .Sum(fourbitcla_2_sum), .cout(cout));
  Multiplexer #(.select(4), .width(8)) multiplexer_3 (
    .in0({fourbitcla_2_sum, fourbitcla_1_sum}), .in1({fourbitcla_2_sum, fourbitcla_1_sum}), .in2(and_1_out),
    .in3(or_1_out), .in4(not_1_out), .in5({A[6:0], 1'b0}), .in6({{2{A[7]}}, A[6:1]}), .in8(A), .in12(B),
    .in13(B), .out(output_a), .sel(ALUop));  // open: in7, in9, in10, in11, in14, in15
  nor nor_1 (Z, output_a[0], output_a[1], output_a[2], output_a[3], output_a[4], output_a[5], output_a[6], output_a[7]);

  // Other names for the same wires on the sheet: ALUop_t = ALUop[0]

  // Notes on the sheet:
  //   ADD/SUB
  //   AND
  //   OR
  //   NOT
  //   SHL
  //   ASR
  //   MOV
  //   ST
  //   LD
endmodule

module Display_Decoder (
  input  En,
  input  [3:0] input_a,
  output FF,
  output FE,
  output FD,
  output FC,
  output FB,
  output FA,
  output F9,
  output F8,
  output F7,
  output F6,
  output F5,
  output F4,
  output F3,
  output F2,
  output F1,
  output F0
);

  Decoder #(.select(4)) decoder_1 (
    .out0(F0), .out1(F1), .out2(F2), .out3(F3), .out4(F4), .out5(F5), .out6(F6), .out7(F7), .out8(F8),
    .out9(F9), .out10(FA), .out11(FB), .out12(FC), .out13(FD), .out14(FE), .out15(FF), .sel(input_a), .en(En));
endmodule
